# Fritzing sketch Schaltplan (saved by Fritzing 0.9.2b)
breadboards: 1

parts:
  5V = LM2596 step down module
  12V = DC Power
  1 = Arduino Pro Mini v13
  R1 = Resistor [tolerance=±5% resistance=10k package=THT]
  Q1 = NPN-Transistor [part_number=9024 package="TO92 [THT]"]
  D1 = Schottky Diode [part_number=BAT43 package="300 mil [THT]"]
  R2 = Resistor [tolerance=±5% resistance=2.2k package=THT]
  Antenne = Antenna
  SIM800_V1 = SIM800_V2
  Steuerleitung = male pin header, 1 pin [form="♂ (male)"]  # not connected
  3A = FUSE [package=fuse_5mm]

nets:
  N1: 5V.IN+, 3A.2
  GND: 5V.IN-, 5V.OUT-, 12V.V-, 1.GND/1, 1.GND/3, Q1.E, SIM800_V1.2, SIM800_V1.6
  N2: 5V.OUT+, 1.VCC, 1.12, SIM800_V1.1, SIM800_V1.3
  N3: 12V.V+, 3A.1
  N4: 1.5, R1.Pin_0
  N5: 1.4, SIM800_V1.4
  N6: 1.3, SIM800_V1.5
  N7: R1.Pin_1, Q1.B, D1.anode
  N8: Q1.C, D1.cathode, R2.Pin_0
  N9: Antenne.antenna_lead, SIM800_V1.8

notes:
  Control Unit

custom parts:
  LM2596 step down module: LM2596 DC-DC step down power supply module 3 A.
  DC Power: A generic dc power symbol
  Arduino Pro Mini v13: It's blue! It's thin! It's the Arduino Pro Mini! SparkFun's minimal design approach to Arduino. This is a 5V Arduino running the 16MHz bootloader. Arduino Pro Mini does not come with connectors populated so that you can solder in any connector or wire with any orientation you need. We recommend first time Arduino users start with the Uno R3. It's a great board that will get you up and running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
  SIM800_V2: SIM Modul
